# Fritzing sketch PWN (saved by Fritzing 0.9.3b)
breadboards: 1

parts:
  LED1 = smd LED [color="Red (633nm)" package="1206 [SMD]"]
  Componente1 = Arduino Uno (Rev3)
  R1 = Resistor [tolerance=±1% resistance=1k package="2010 [SMD]"]
  D1 = Rectifier Diode [part_number=1N4001 package="300 mil [THT]"]  # not connected
  Q1 = npn-Powertransistor [package="TO220 [THT]"]
  R2 = Resistor [tolerance=±1% resistance=1k package="2010 [SMD]"]  # not connected
  VCC1 = 4 x AAA Battery Mount
  M1 = DC Motor

nets:
  N1: LED1.anode, Componente1.D11_PWM/MOSI
  N2: Componente1.GND, Q1.emitter, VCC1.-
  N3: Componente1.D3_PWM, R1.Pin_0
  N4: R1.Pin_1, Q1.base
  N5: Q1.collector, M1.pin_2
