# Fritzing sketch SuperMaquina (saved by Fritzing 0.9.3b)
breadboards: 1

parts:
  LED1 = LED - 5mm [color="Red (633nm)" package="5 mm [THT]"]
  Componente1 = Arduino Uno (Rev3)
  R1 = Resistor [tolerance=±5% resistance=330 package=THT]
  R2 = Resistor [tolerance=±5% resistance=220 package=THT]
  LED2 = LED - 5mm [color="Red (633nm)" package="5 mm [THT]"]
  R3 = Resistor [tolerance=±5% resistance=220 package=THT]
  LED3 = LED - 5mm [color="Red (633nm)" package="5 mm [THT]"]
  R4 = Resistor [tolerance=±5% resistance=220 package=THT]
  LED4 = LED - 5mm [color="Red (633nm)" package="5 mm [THT]"]
  R5 = Resistor [tolerance=±5% resistance=220 package=THT]
  LED5 = LED - 5mm [color="Red (633nm)" package="5 mm [THT]"]
  R6 = Resistor [tolerance=±5% resistance=220 package=THT]
  LED6 = LED - 5mm [color="Red (633nm)" package="5 mm [THT]"]

nets:
  N1: LED1.cathode, R1.Pin_0
  N2: LED1.anode, Componente1.D13/SCK
  N3: Componente1.D8, LED6.anode
  N4: Componente1.D9_PWM, LED5.anode
  N5: Componente1.D10_PWM/SS, LED4.anode
  N6: Componente1.D11_PWM/MOSI, LED3.anode
  N7: Componente1.D12/MISO, LED2.anode
  N8: Componente1.GND, R1.Pin_1, R2.Pin_1, R3.Pin_1, R4.Pin_1, R5.Pin_1, R6.Pin_1
  N9: R2.Pin_0, LED2.cathode
  N10: R3.Pin_0, LED3.cathode
  N11: R4.Pin_0, LED4.cathode
  N12: R5.Pin_0, LED5.cathode
  N13: R6.Pin_0, LED6.cathode

// code stored in the sketch: Super_M_quina.ino
/**
   Sequencial de LEDs (efeito supermáquina)
   @author: Carlos Eduardo
   /
*/
void setup() {
  pinMode (13, OUTPUT);

}

void loop() {
  digitalWrite (13, HIGH);

}
