# Fritzing sketch atomacaofinal (saved by Fritzing 0.9.3b)
breadboards: 1

parts:
  Componente1 = Arduino Uno (Rev3)
  LED1 = LED - 5mm [color="Red (633nm)" package="5 mm [THT]"]
  R1 = Resistor [tolerance=±5% resistance=220 package=THT]
  Componente2 = Bluetooth HC-05 Macho
  R3 = Resistor [tolerance=±5% resistance=2.2k package=THT]
  R4 = Resistor [tolerance=±5% resistance=1k package=THT]
  Q1 = Basic FET P-Channel [package="TO220 [THT]"]
  R7 = Resistor [tolerance=±5% resistance=1k package=THT]
  D1 = Rectifier Diode [part_number=1N4001 package="300 mil [THT]"]
  OMRON1 = OMRON PCB Power Relay – G5LE [part_number="G5LE-1\n" package=THT]

nets:
  N1: Componente1.D13/SCK, LED1.anode
  N2: Componente1.D0/RX, Componente2.TXD
  N3: Componente1.D1/TX, R4.Pin_0
  5V: Componente1.5V, Componente2.VCC, D1.cathode, OMRON1.COIL1
  GND: Componente1.GND, R1.Pin_1, Componente2.GND, R3.Pin_1, Q1.drain, D1.anode, OMRON1.COIL2
  N4: LED1.cathode, R1.Pin_0
  N5: Componente2.RXD, R3.Pin_0, R4.Pin_1
  N6: Q1.gate, R7.Pin_1
