# Fritzing sketch pwm_Sketch (saved by Fritzing 0.9.3b)
breadboards: 1

parts:
  LED1 = LED - 5mm [color="Red (633nm)" package="5 mm [THT]"]
  Q2 = npn-Powertransistor [package="TO220 [THT]"]
  R1 = Resistor [tolerance=±5% resistance=1k package=THT]
  R2 = Resistor [tolerance=±5% resistance=220 package=THT]
  Componente1 = Arduino Uno (Rev3)
  D1 = Rectifier Diode [part_number=1N4001 package="300 mil [THT]"]
  M1 = DC Motor
  VCC1 = 4 x AAA Battery Mount

nets:
  N1: LED1.cathode, R2.Pin_0
  N2: LED1.anode, Componente1.D11_PWM/MOSI
  N3: Q2.base, R1.Pin_1
  N4: Q2.collector, D1.anode, M1.pin_2
  N5: Q2.emitter, R2.Pin_1, Componente1.GND
  N6: R1.Pin_0, Componente1.D3_PWM
  N7: D1.cathode, M1.pin_1, VCC1.+
