# Fritzing sketch sensor_Luminosidade0210 (saved by Fritzing 0.9.3b)
breadboards: 1

parts:
  Componente1 = Arduino Uno (Rev3)
  R1 = Resistor [tolerance=±5% resistance=10k package=THT]  # not connected
  R2 = Photocell (LDR) [package=THT]
  R3 = Resistor [tolerance=±5% resistance=100k package=THT]
  LED1 = LED - 5mm [color="Red (633nm)" package="5 mm [THT]"]

nets:
  N1: Componente1.A0, R2.pin_0
  N2: Componente1.D3_PWM, LED1.anode
  N3: Componente1.5V, R2.pin_1
  N4: Componente1.GND, R3.Pin_0
  N5: R3.Pin_1, LED1.cathode
